# Fritzing sketch Scheme (saved by Fritzing 0.9.5d)

parts:
  Компонент1 = Arduino Uno (Rev3)
  S1 = Round Pushbutton
  S2 = Round Pushbutton
  S3 = Round Pushbutton
  S4 = Round Pushbutton
  U1 = NodeMCU V3.0
  U2 = NodeMCU V3.0
  Компонент2 = InvenSense MPU6050
  U3 = LIPO-110mAh [package=lipo-110]
  A1 = DM860A Stepper Motor Driver
  A2 = DM860A Stepper Motor Driver
  M1 = Stepper Motor - Bipolar
  M2 = Stepper Motor - Bipolar
  PWM1 = PCA9685 16x12-bit PWM Breakout

nets:
  N1: Компонент1.A4/SDA, PWM1.no_name_yet#503
  N2: Компонент1.A5/SCL, PWM1.no_name_yet#504
  N3: Компонент1.D9_PWM, A1.DIR+(+5V)
  N4: Компонент1.D10_PWM/SS, A1.ENBL+(+5V)
  N5: Компонент1.D11_PWM/MOSI, A2.ENBL+(+5V)
  N6: Компонент1.D12/MISO, A2.DIR+(+5V)
  N7: Компонент1.D2, S3.leg0, S4.leg0
  N8: Компонент1.D3_PWM, S1.leg1, S2.leg1
  N9: Компонент1.D4, U2.RX
  N10: Компонент1.D5_PWM, U2.TX
  N11: Компонент1.GND, S1.leg0, S2.leg0, S3.leg1, S4.leg1
  N12: U1.D1, Компонент2.SCL
  N13: U1.D2, Компонент2.SDA
  GND: U1.GND, Компонент2.GND, U3.-
  3V3: U1.3V3, Компонент2.VCC
  N14: U1.Vin, U3.+
  N15: A1.B-, M1.D
  N16: A1.B+, M1.B
  N17: A1.A-, M1.C
  N18: A1.A+, M1.A
  N19: A1.ENBL-(ENB), A1.PUL-(PUL)
  N20: A1.PUL+(+5V), PWM1.no_name_yet#4
  N21: A2.B-, M2.D
  N22: A2.B+, M2.B
  N23: A2.A-, M2.C
  N24: A2.A+, M2.A
  N25: A2.ENBL-(ENB), A2.PUL-(PUL)
  N26: A2.PUL+(+5V), PWM1.no_name_yet#0
  N27: PWM1.no_name_yet#501, PWM1.no_name_yet#701

custom parts:
  NodeMCU V3.0: ESP8266 based NodeMCU
  DM860A Stepper Motor Driver: DM860A is a type of two-phase hybrid stepping motor driver, The drive voltage of which is from 24VDC to 80VDC. It is designed for use with 2-phase hybrid stepper motor of all kinds with 57mm to 110mm outside diameter and less than 8.0A phase current. Mar 2023: Correct pcb layerId as the part won't save correctly in a .fzz file as is.
